// Logisim project 1306180022.circ as structural Verilog: 1 circuit, main circuit main
module main (
  input  X3,
  input  X2,
  input  X1
);

  wire and_1_out, and_2_out, and_3_out, and_4_out, and_5_out, and_6_out, and_7_out, and_8_out, and_9_out,
       and_10_out, and_11_out, and_12_out, and_13_out, and_14_out, and_15_out, and_16_out, and_17_out,
       and_18_out, and_19_out, and_20_out, and_21_out, and_22_out, and_23_out, and_24_out, and_25_out,
       and_26_out, and_27_out, and_28_out, and_29_out, and_30_out, and_31_out, and_32_out, and_33_out,
       clock_1_out, D1_q, D2_q, D3_q, not_1_out, not_2_out, not_3_out, not_4_out, not_5_out, not_6_out,
       not_7_out, not_8_out, not_9_out, not_10_out, not_11_out, not_12_out, not_13_out, not_14_out,
       not_15_out, not_16_out, not_17_out, not_18_out, not_19_out, not_20_out, not_21_out, not_22_out,
       not_23_out, not_24_out, not_25_out, not_26_out, not_27_out, not_28_out, not_29_out, not_30_out,
       not_31_out, not_32_out, not_33_out, not_34_out, not_35_out, not_36_out, not_37_out, not_38_out,
       not_39_out, not_40_out, not_41_out, or_1_out, or_2_out, or_3_out, or_4_out, or_5_out, or_6_out,
       or_7_out, or_8_out, or_9_out;

  not not_1 (not_1_out, X3);
  not not_2 (not_2_out, D3_q);
  not not_3 (not_3_out, X3);
  not not_4 (not_4_out, D1_q);
  not not_5 (not_5_out, D1_q);
  not not_6 (not_6_out, D2_q);
  not not_7 (not_7_out, X1);
  not not_8 (not_8_out, D2_q);
  not not_9 (not_9_out, X3);
  not not_10 (not_10_out, X2);
  not not_11 (not_11_out, X3);
  not not_12 (not_12_out, D1_q);
  not not_13 (not_13_out, D3_q);
  not not_14 (not_14_out, D1_q);
  not not_15 (not_15_out, X3);
  not not_16 (not_16_out, D2_q);
  not not_17 (not_17_out, D3_q);
  not not_18 (not_18_out, D2_q);
  not not_19 (not_19_out, X1);
  not not_20 (not_20_out, X3);
  not not_21 (not_21_out, X1);
  not not_22 (not_22_out, D2_q);
  not not_23 (not_23_out, D3_q);
  not not_24 (not_24_out, X3);
  not not_25 (not_25_out, D1_q);
  not not_26 (not_26_out, X1);
  not not_27 (not_27_out, D1_q);
  not not_28 (not_28_out, D2_q);
  not not_29 (not_29_out, D1_q);
  not not_30 (not_30_out, D3_q);
  not not_31 (not_31_out, D1_q);
  not not_32 (not_32_out, X2);
  not not_33 (not_33_out, X3);
  not not_34 (not_34_out, X2);
  not not_35 (not_35_out, D2_q);
  not not_36 (not_36_out, X2);
  not not_37 (not_37_out, X1);
  not not_38 (not_38_out, D1_q);
  not not_39 (not_39_out, D3_q);
  not not_40 (not_40_out, D2_q);
  not not_41 (not_41_out, D1_q);
  and and_1 (and_1_out, not_1_out, D3_q, D3_q, D3_q);
  and and_2 (and_2_out, X3, not_2_out);
  and and_3 (and_3_out, not_3_out, not_4_out);
  and and_4 (and_4_out, D2_q, D1_q);
  and and_5 (and_5_out, not_5_out, not_6_out);
  and and_6 (and_6_out, not_7_out, D3_q);
  and and_7 (and_7_out, X2, D3_q, not_8_out);
  and and_8 (and_8_out, not_9_out, D1_q);
  and and_9 (and_9_out, D1_q, D3_q);
  and and_10 (and_10_out, not_10_out, X1, not_11_out);
  and and_11 (and_11_out, X1, D2_q, not_12_out);
  and and_12 (and_12_out, X3, not_13_out, not_14_out);
  and and_13 (and_13_out, not_15_out, not_16_out);
  and and_14 (and_14_out, X1, D2_q, D3_q);
  and and_15 (and_15_out, X3, not_17_out, not_18_out);
  and and_16 (and_16_out, not_19_out, not_20_out);
  and and_17 (and_17_out, X2, not_21_out);
  and and_18 (and_18_out, D3_q, not_22_out);
  and and_19 (and_19_out, not_23_out, D2_q);
  and and_20 (and_20_out, not_24_out, not_25_out);
  and and_21 (and_21_out, not_26_out, D3_q, not_27_out);
  and and_22 (and_22_out, X2, not_28_out, not_29_out);
  and and_23 (and_23_out, X3, not_30_out, not_31_out);
  and and_24 (and_24_out, not_32_out, X1);
  and and_25 (and_25_out, X1, D2_q, D3_q);
  and and_26 (and_26_out, not_33_out, X2, X1);
  and and_27 (and_27_out, not_34_out, X1, D3_q, not_35_out);
  and and_28 (and_28_out, X2, D3_q, D1_q);
  and and_29 (and_29_out, X3, D1_q, D2_q);
  and and_30 (and_30_out, not_36_out, not_37_out, D3_q);
  and and_31 (and_31_out, X2, not_38_out);
  and and_32 (and_32_out, not_39_out, not_40_out, D1_q);
  and and_33 (and_33_out, D2_q, not_41_out);
  or or_1 (or_1_out, and_1_out, and_2_out);
  or or_2 (or_2_out, and_3_out, and_4_out, and_5_out, and_6_out, and_7_out);
  LED led_1 (.in(D2_q));
  LED led_2 (.in(D1_q));
  Clock clock_1 (.out(clock_1_out));
  or or_3 (or_3_out, and_8_out, and_9_out, and_10_out, and_11_out, and_12_out);
  or or_4 (or_4_out, and_13_out, and_14_out);
  or or_5 (or_5_out, and_16_out, and_17_out, and_18_out, and_19_out);
  or or_6 (or_6_out, and_20_out, and_21_out, and_22_out);
  or or_7 (or_7_out, and_24_out, and_25_out, D1_q);
  or or_8 (or_8_out, and_26_out, and_27_out, and_28_out);
  or or_9 (or_9_out, and_30_out, and_31_out, and_32_out, and_33_out);
  LED led_3 (.in(D3_q));
  D_Flip_Flop D1 (.clk(clock_1_out), .D(or_1_out), .Q(D1_q));  // open: Qn, preset, en, reset
  D_Flip_Flop D2 (.clk(clock_1_out), .D(or_2_out), .Q(D2_q));  // open: Qn, preset, en, reset
  D_Flip_Flop D3 (.clk(clock_1_out), .D(or_3_out), .Q(D3_q));  // open: Qn, preset, en, reset
  LED Y1 (.in(or_4_out));
  LED S1 (.in(and_15_out));
  LED K1 (.in(or_5_out));
  LED Y2 (.in(or_6_out));
  LED S2 (.in(and_23_out));
  LED led_4 (.in(or_7_out));
  LED Y3 (.in(or_8_out));
  LED S3 (.in(and_29_out));
  LED K3 (.in(or_9_out));
endmodule
